# Fritzing sketch cybergarden (saved by Fritzing 0.9.3b)
breadboards: 1

parts:
  RHT1 = Humidity and Temperature Sensor RHT03
  R1 = Resistor [tolerance=±5% resistance=10k package="2010 [SMD]"]
  Part2 = Arduino Leonardo (Rev3b)

nets:
  VCC: RHT1.Vcc, R1.Pin_1, Part2.3V3
  N1: RHT1.Data-signal, Part2.GND
  N2: RHT1.GND_1, Part2.D13_PWM
  N3: RHT1.GND_2, R1.Pin_0, Part2.D1/TX

notes:
  Temperature/Humidity Sensor (SHT10)
